// Logisim project cpu.circ as structural Verilog: 29 circuits, main circuit cpu
module main (
  input  in_1,
  input  in_2,
  input  in_3,
  output out_4
);

  ripple_adder_8 ripple_adder_8_1 ();  // open: a, b, c, sum, carry
  reg_8 reg_8_1 ();  // open: data, store, clk, out_4
  mux_4_1_8 mux_4_1_8_1 ();  // open: a, b, c, d, sel0, sel1, out_7
  alu_8 alu_8_1 ();  // open: a, b, inc_b, inv_b, zero_b, s0, s1, out_8, carry
  Register #(.width(1)) register_1 (.D(in_1), .en(in_2), .clk(in_3), .Q(out_4), .clr(1'b0));

  // Notes on the sheet:
  //   data is only changed when clk changes from 0 to 1; my reg is different
endmodule

module my_xor (
  input  a,
  input  b,
  output o
);

  wire and_1_out, and_2_out, not_1_out, not_2_out;

  not not_1 (not_1_out, a);
  not not_2 (not_2_out, b);
  and and_1 (and_1_out, not_1_out, b);
  and and_2 (and_2_out, a, not_2_out);
  or or_1 (o, and_1_out, and_2_out);

  // Notes on the sheet:
  //   XOR circuit built using Logisim
endmodule

module half_adder (
  input  a,
  input  b,
  output sum,
  output carry
);

  xor xor_1 (sum, a, b);
  and and_1 (carry, a, b);
endmodule

module full_adder (
  input  a,
  input  b,
  input  c,
  output sum,
  output carry
);

  wire half_adder_1_carry, half_adder_1_sum, half_adder_2_carry;

  half_adder half_adder_1 (.a(a), .b(b), .sum(half_adder_1_sum), .carry(half_adder_1_carry));
  half_adder half_adder_2 (.a(half_adder_1_sum), .b(c), .sum(sum), .carry(half_adder_2_carry));
  or or_1 (carry, half_adder_1_carry, half_adder_2_carry);
endmodule

module ripple_adder_8 (
  input  [7:0] a,
  input  [7:0] b,
  input  c,
  output [7:0] sum,
  output carry
);

  wire full_adder_1_carry, full_adder_2_carry, full_adder_3_carry, full_adder_4_carry, full_adder_5_carry,
       full_adder_6_carry, full_adder_7_carry;

  full_adder full_adder_1 (.a(a[0]), .b(b[0]), .c(c), .sum(sum[0]), .carry(full_adder_1_carry));
  full_adder full_adder_2 (.a(a[1]), .b(b[1]), .c(full_adder_1_carry), .sum(sum[1]), .carry(full_adder_2_carry));
  full_adder full_adder_3 (.a(a[2]), .b(b[2]), .c(full_adder_2_carry), .sum(sum[2]), .carry(full_adder_3_carry));
  full_adder full_adder_4 (.a(a[3]), .b(b[3]), .c(full_adder_3_carry), .sum(sum[3]), .carry(full_adder_4_carry));
  full_adder full_adder_5 (.a(a[4]), .b(b[4]), .c(full_adder_4_carry), .sum(sum[4]), .carry(full_adder_5_carry));
  full_adder full_adder_6 (.a(a[5]), .b(b[5]), .c(full_adder_5_carry), .sum(sum[5]), .carry(full_adder_6_carry));
  full_adder full_adder_7 (.a(a[6]), .b(b[6]), .c(full_adder_6_carry), .sum(sum[6]), .carry(full_adder_7_carry));
  full_adder full_adder_8 (.a(a[7]), .b(b[7]), .c(full_adder_7_carry), .sum(sum[7]), .carry(carry));
endmodule

module ripple_adder_16 (
  input  [15:0] a,
  input  [15:0] b,
  input  carry_in,
  output [15:0] sum,
  output carry_out
);

  wire ripple_adder_8_1_carry;

  ripple_adder_8 ripple_adder_8_1 (
    .a(a[7:0]), .b(b[7:0]), .c(carry_in), .sum(sum[7:0]), .carry(ripple_adder_8_1_carry));
  ripple_adder_8 ripple_adder_8_2 (
    .a(a[15:8]), .b(b[15:8]), .c(ripple_adder_8_1_carry), .sum(sum[15:8]), .carry(carry_out));
endmodule

module mux_2_1_1 (
  input  a,
  input  b,
  input  sel,
  output out_4
);

  wire and_1_out, and_2_out, not_1_out;

  not not_1 (not_1_out, sel);
  and and_1 (and_1_out, a, not_1_out);
  and and_2 (and_2_out, b, sel);
  or or_1 (out_4, and_1_out, and_2_out);
endmodule

module mux_2_1_8 (
  input  [7:0] a,
  input  [7:0] b,
  input  sel,
  output [7:0] out_4
);

  mux_2_1_1 mux_2_1_1_1 (.a(a[0]), .b(b[0]), .sel(sel), .out_4(out_4[0]));
  mux_2_1_1 mux_2_1_1_2 (.a(a[1]), .b(b[1]), .sel(sel), .out_4(out_4[1]));
  mux_2_1_1 mux_2_1_1_3 (.a(a[2]), .b(b[2]), .sel(sel), .out_4(out_4[2]));
  mux_2_1_1 mux_2_1_1_4 (.a(a[3]), .b(b[3]), .sel(sel), .out_4(out_4[3]));
  mux_2_1_1 mux_2_1_1_5 (.a(a[4]), .b(b[4]), .sel(sel), .out_4(out_4[4]));
  mux_2_1_1 mux_2_1_1_6 (.a(a[5]), .b(b[5]), .sel(sel), .out_4(out_4[5]));
  mux_2_1_1 mux_2_1_1_7 (.a(a[6]), .b(b[6]), .sel(sel), .out_4(out_4[6]));
  mux_2_1_1 mux_2_1_1_8 (.a(a[7]), .b(b[7]), .sel(sel), .out_4(out_4[7]));
endmodule

module mux_4_1_8 (
  input  [7:0] a,
  input  [7:0] b,
  input  [7:0] c,
  input  [7:0] d,
  input  sel0,
  input  sel1,
  output [7:0] out_7
);

  wire [7:0] mux_2_1_8_1_out_4, mux_2_1_8_2_out_4;

  mux_2_1_8 mux_2_1_8_1 (.a(a), .b(b), .sel(sel0), .out_4(mux_2_1_8_1_out_4));
  mux_2_1_8 mux_2_1_8_2 (.a(c), .b(d), .sel(sel0), .out_4(mux_2_1_8_2_out_4));
  mux_2_1_8 mux_2_1_8_3 (.a(mux_2_1_8_1_out_4), .b(mux_2_1_8_2_out_4), .sel(sel1), .out_4(out_7));
endmodule

module gated_D_latch (
  input  data,
  input  store,
  output q
);

  wire and_1_out, and_2_out, not_1_out, not_3_out, or_1_out, or_2_out;

  not not_1 (not_1_out, data);
  and and_1 (and_1_out, not_1_out, store);
  and and_2 (and_2_out, store, data);
  not not_2 (q, or_1_out);
  or or_1 (or_1_out, and_1_out, not_3_out);
  not not_3 (not_3_out, or_2_out);
  or or_2 (or_2_out, q, and_2_out);
endmodule

module D_flip_flop (
  input  data,
  input  store,
  input  clk,
  output o
);

  wire and_1_out, gated_d_latch_1_q, not_1_out;

  and and_1 (and_1_out, store, not_1_out);
  not not_1 (not_1_out, clk);
  gated_D_latch gated_d_latch_1 (.data(data), .store(and_1_out), .q(gated_d_latch_1_q));
  gated_D_latch gated_d_latch_2 (.data(gated_d_latch_1_q), .store(clk), .q(o));
endmodule

module alu_8 (
  input  [7:0] a,
  input  [7:0] b,
  input  inc_b,
  input  inv_b,
  input  zero_b,
  input  s0,
  input  s1,
  output [7:0] out_8,
  output carry
);

  wire not_1_out;
  wire [7:0] and_1_out, and_2_out, rep_8_1_out_2, rep_8_2_out_2, ripple_adder_8_1_sum, xor_1_out;

  not not_1 (not_1_out, zero_b);
  rep_8 rep_8_1 (.in_1(not_1_out), .out_2(rep_8_1_out_2));
  rep_8 rep_8_2 (.in_1(inv_b), .out_2(rep_8_2_out_2));
  assign xor_1_out = b ^ rep_8_2_out_2;  // XOR_Gate xor_1, 8 bits wide
  assign and_1_out = xor_1_out & rep_8_1_out_2;  // AND_Gate and_1, 8 bits wide
  ripple_adder_8 ripple_adder_8_1 (.a(a), .b(and_1_out), .c(inc_b), .sum(ripple_adder_8_1_sum), .carry(carry));
  assign and_2_out = a & b;  // AND_Gate and_2, 8 bits wide
  mux_4_1_8 mux_4_1_8_1 (.a(ripple_adder_8_1_sum), .b(and_2_out), .c(a), .d(b), .sel0(s0), .sel1(s1), .out_7(out_8));
endmodule

module rep_8 (
  input  in_1,
  output [7:0] out_2
);


  assign out_2 = {8{in_1}};

  // Notes on the sheet:
  //   bit extender is not working as expecte so I created my version
endmodule

module rep_13 (
  input  in_1,
  output [12:0] out_2
);


  assign out_2 = {13{in_1}};
endmodule

module demux_1_2_1 (
  input  data,
  input  sel,
  output o0,
  output o1
);

  wire not_1_out;

  not not_1 (not_1_out, sel);
  and and_1 (o0, data, not_1_out);
  and and_2 (o1, data, sel);
endmodule

module reg_8 (
  input  [7:0] data,
  input  store,
  input  clk,
  output [7:0] out_4
);

  D_flip_flop d_flip_flop_1 (.data(data[0]), .store(store), .clk(clk), .o(out_4[0]));
  D_flip_flop d_flip_flop_2 (.data(data[1]), .store(store), .clk(clk), .o(out_4[1]));
  D_flip_flop d_flip_flop_3 (.data(data[2]), .store(store), .clk(clk), .o(out_4[2]));
  D_flip_flop d_flip_flop_4 (.data(data[3]), .store(store), .clk(clk), .o(out_4[3]));
  D_flip_flop d_flip_flop_5 (.data(data[4]), .store(store), .clk(clk), .o(out_4[4]));
  D_flip_flop d_flip_flop_6 (.data(data[5]), .store(store), .clk(clk), .o(out_4[5]));
  D_flip_flop d_flip_flop_7 (.data(data[6]), .store(store), .clk(clk), .o(out_4[6]));
  D_flip_flop d_flip_flop_8 (.data(data[7]), .store(store), .clk(clk), .o(out_4[7]));
endmodule

module ram_4_reg8 (
  input  clk,
  input  [7:0] data,
  input  store,
  input  [2:0] address,
  output [7:0] out_5
);

  wire demultiplexer_1_out0, demultiplexer_1_out1, demultiplexer_1_out2, demultiplexer_1_out3,
       demultiplexer_1_out4, demultiplexer_1_out5, demultiplexer_1_out6, demultiplexer_1_out7;
  wire [7:0] reg_8_1_out_4, reg_8_2_out_4, reg_8_3_out_4, reg_8_4_out_4, reg_8_5_out_4, reg_8_6_out_4,
       reg_8_7_out_4, reg_8_8_out_4;

  Demultiplexer #(.select(3), .enable("false")) demultiplexer_1 (
    .out0(demultiplexer_1_out0), .out1(demultiplexer_1_out1), .out2(demultiplexer_1_out2),
    .out3(demultiplexer_1_out3), .out4(demultiplexer_1_out4), .out5(demultiplexer_1_out5),
    .out6(demultiplexer_1_out6), .out7(demultiplexer_1_out7), .in(store), .sel(address));
  reg_8 reg_8_1 (.data(data), .store(demultiplexer_1_out0), .clk(clk), .out_4(reg_8_1_out_4));
  reg_8 reg_8_2 (.data(data), .store(demultiplexer_1_out1), .clk(clk), .out_4(reg_8_2_out_4));
  reg_8 reg_8_3 (.data(data), .store(demultiplexer_1_out2), .clk(clk), .out_4(reg_8_3_out_4));
  reg_8 reg_8_4 (.data(data), .store(demultiplexer_1_out3), .clk(clk), .out_4(reg_8_4_out_4));
  reg_8 reg_8_5 (.data(data), .store(demultiplexer_1_out4), .clk(clk), .out_4(reg_8_5_out_4));
  reg_8 reg_8_6 (.data(data), .store(demultiplexer_1_out5), .clk(clk), .out_4(reg_8_6_out_4));
  reg_8 reg_8_7 (.data(data), .store(demultiplexer_1_out6), .clk(clk), .out_4(reg_8_7_out_4));
  reg_8 reg_8_8 (.data(data), .store(demultiplexer_1_out7), .clk(clk), .out_4(reg_8_8_out_4));
  Multiplexer #(.select(3), .width(8), .enable("false")) multiplexer_1 (
    .in0(reg_8_1_out_4), .in1(reg_8_2_out_4), .in2(reg_8_3_out_4), .in3(reg_8_4_out_4), .in4(reg_8_5_out_4),
    .in5(reg_8_6_out_4), .in6(reg_8_7_out_4), .in7(reg_8_8_out_4), .out(out_5), .sel(address));
endmodule

module cpu_incrementer (
  input  [15:0] value,
  output [15:0] o
);

  ripple_adder_16 ripple_adder_16_1 (.a(value), .b({16{1'b0}}), .carry_in(1'b1), .sum(o));  // open: carry_out
endmodule

module cpu_counter (
  input  [15:0] value,
  input  clk,
  input  store,
  output [15:0] o
);

  wire [15:0] cpu_incrementer_1_o, multiplexer_1_out;

  Multiplexer #(.width(16), .enable("false")) multiplexer_1 (
    .in0(cpu_incrementer_1_o), .in1(value), .out(multiplexer_1_out), .sel(store));
  Register #(.width(16)) register_1 (.D(multiplexer_1_out), .en(1'b1), .clk(clk), .Q(o), .clr(1'b0));
  cpu_incrementer cpu_incrementer_1 (.value(o), .o(cpu_incrementer_1_o));
endmodule

module cpu_zero (
  input  [15:0] value,
  output is_zero
);

  wire and_1_out, and_2_out, and_3_out, and_4_out, and_5_out, and_6_out, nor_1_out, nor_2_out, nor_3_out,
       nor_4_out, nor_5_out, nor_6_out, nor_7_out, nor_8_out;

  nor nor_1 (nor_1_out, value[0], value[1]);
  nor nor_2 (nor_2_out, value[2], value[3]);
  nor nor_3 (nor_3_out, value[4], value[5]);
  nor nor_4 (nor_4_out, value[6], value[7]);
  nor nor_5 (nor_5_out, value[8], value[9]);
  nor nor_6 (nor_6_out, value[10], value[11]);
  nor nor_7 (nor_7_out, value[12], value[13]);
  nor nor_8 (nor_8_out, value[14], value[15]);
  and and_1 (and_1_out, nor_7_out, nor_8_out);
  and and_2 (and_2_out, nor_1_out, nor_2_out);
  and and_3 (and_3_out, nor_3_out, nor_4_out);
  and and_4 (and_4_out, nor_5_out, nor_6_out);
  and and_5 (and_5_out, and_2_out, and_3_out);
  and and_6 (and_6_out, and_4_out, and_1_out);
  and and_7 (is_zero, and_5_out, and_6_out);
endmodule

module cpu_less_0 (
  input  [15:0] value,
  output less_0
);


  assign less_0 = value[15];
endmodule

module cpu_unary_alu (
  input  zero,
  input  invert,
  input  [15:0] value,
  output [15:0] o
);

  wire [15:0] multiplexer_1_out, not_1_out;

  Multiplexer #(.width(16), .enable("false")) multiplexer_1 (
    .in0(value), .in1({16{1'b0}}), .out(multiplexer_1_out), .sel(zero));
  assign not_1_out = ~multiplexer_1_out;  // NOT_Gate not_1, 16 bits wide
  Multiplexer #(.width(16), .enable("false")) multiplexer_2 (
    .in0(multiplexer_1_out), .in1(not_1_out), .out(o), .sel(invert));
endmodule

module cpu_alu (
  input  [15:0] X,
  input  [15:0] Y,
  input  zero_X,
  input  inv_X,
  input  zero_Y,
  input  inv_Y,
  input  op,
  input  inv_out,
  output [15:0] output_value
);

  wire [15:0] and_1_out, cpu_unary_alu_1_o, cpu_unary_alu_2_o, multiplexer_1_out, not_1_out,
       ripple_adder_16_1_sum;

  cpu_unary_alu cpu_unary_alu_1 (.zero(zero_X), .invert(inv_X), .value(X), .o(cpu_unary_alu_1_o));
  cpu_unary_alu cpu_unary_alu_2 (.zero(zero_Y), .invert(inv_Y), .value(Y), .o(cpu_unary_alu_2_o));
  assign and_1_out = cpu_unary_alu_1_o & cpu_unary_alu_2_o;  // AND_Gate and_1, 16 bits wide
  Multiplexer #(.width(16), .enable("false")) multiplexer_1 (
    .in0(and_1_out), .in1(ripple_adder_16_1_sum), .out(multiplexer_1_out), .sel(op));
  ripple_adder_16 ripple_adder_16_1 (
    .a(cpu_unary_alu_1_o), .b(cpu_unary_alu_2_o), .sum(ripple_adder_16_1_sum));  // open: carry_in, carry_out
  Multiplexer #(.width(16), .enable("false")) multiplexer_2 (
    .in0(multiplexer_1_out), .in1(not_1_out), .out(output_value), .sel(inv_out));
  assign not_1_out = ~multiplexer_1_out;  // NOT_Gate not_1, 16 bits wide
endmodule

module cpu_condition (
  input  [15:0] value,
  input  less_0,
  input  equal_0,
  input  greater_0,
  output jump
);

  wire and_1_out, and_2_out, and_3_out, cpu_less_0_1_less_0, cpu_zero_1_is_zero, not_1_out, not_2_out;

  cpu_less_0 cpu_less_0_1 (.value(value), .less_0(cpu_less_0_1_less_0));
  cpu_zero cpu_zero_1 (.value(value), .is_zero(cpu_zero_1_is_zero));
  and and_1 (and_1_out, cpu_less_0_1_less_0, less_0);
  not not_1 (not_1_out, cpu_zero_1_is_zero);
  not not_2 (not_2_out, cpu_less_0_1_less_0);
  and and_2 (and_2_out, cpu_zero_1_is_zero, equal_0);
  and and_3 (and_3_out, not_1_out, not_2_out, greater_0);
  or or_1 (jump, and_1_out, and_2_out, and_3_out);
endmodule

module cpu_memory_unit (
  input  write_to_A,
  input  write_to_D,
  input  write_to_RAM_at_A,
  input  [15:0] value,
  input  clk,
  output [15:0] out_A,
  output [15:0] out_D,
  output [15:0] RAM_at_A
);

  Register #(.width(16)) A (.D(value), .en(write_to_A), .clk(clk), .Q(out_A));  // open: clr
  RAM #(.addrWidth(16), .dataWidth(16), .databus("bibus")) ram_1 (
    .addr(out_A), .we(write_to_RAM_at_A), .oe(1'b1), .clk(clk), .din(value), .dout(RAM_at_A));
  Register #(.width(16)) D (.D(value), .en(write_to_D), .clk(clk), .Q(out_D));  // open: clr
endmodule

module cpu_i_decoder (
  input  [15:0] instr,
  output jmp_if_ALU_out_is_less_0,
  output jmp_if_ALU_out_is_0,
  output jmp_if_ALU_out_is_greater_0,
  output write_ALU_out_to_RAM_at_A,
  output write_ALU_out_to_D,
  output write_ALU_out_to_A,
  output alu_Y_if_0_A_else_RAM_at_A,
  output zero_X,
  output inv_X,
  output zero_Y,
  output inv_Y,
  output alu_op_if_0_logical_and_else_add,
  output inv_alu_out,
  output compute,
  output [15:0] value
);

  wire not_1_out;
  wire [5:5] and_1_out;
  wire [12:0] rep_13_1_out_2;

  assign {alu_Y_if_0_A_else_RAM_at_A, zero_X, inv_X, zero_Y, inv_Y, alu_op_if_0_logical_and_else_add, inv_alu_out, and_1_out[5], write_ALU_out_to_D, write_ALU_out_to_RAM_at_A, jmp_if_ALU_out_is_greater_0, jmp_if_ALU_out_is_0, jmp_if_ALU_out_is_less_0} = instr[12:0] & rep_13_1_out_2;  // AND_Gate and_1, 13 bits wide
  rep_13 rep_13_1 (.in_1(instr[15]), .out_2(rep_13_1_out_2));
  not not_1 (not_1_out, instr[15]);
  or or_1 (write_ALU_out_to_A, and_1_out[5], not_1_out);

  assign compute = instr[15];
  assign value = instr;
endmodule

module cpu_control_unit (
  input  clk,
  input  [15:0] inst,
  output [15:0] jump_address,
  output jump
);

  wire cpu_i_decoder_1_alu_op_if_0_logical_and_else_add, cpu_i_decoder_1_alu_y_if_0_a_else_ram_at_a,
       cpu_i_decoder_1_compute, cpu_i_decoder_1_inv_alu_out, cpu_i_decoder_1_inv_x, cpu_i_decoder_1_inv_y,
       cpu_i_decoder_1_jmp_if_alu_out_is_0, cpu_i_decoder_1_jmp_if_alu_out_is_greater_0,
       cpu_i_decoder_1_jmp_if_alu_out_is_less_0, cpu_i_decoder_1_write_alu_out_to_a,
       cpu_i_decoder_1_write_alu_out_to_d, cpu_i_decoder_1_write_alu_out_to_ram_at_a, cpu_i_decoder_1_zero_x,
       cpu_i_decoder_1_zero_y;
  wire [15:0] cpu_alu_1_output_value, cpu_i_decoder_1_value, cpu_memory_unit_1_out_d,
       cpu_memory_unit_1_ram_at_a, multiplexer_1_out, multiplexer_2_out;

  cpu_i_decoder cpu_i_decoder_1 (
    .instr(inst), .jmp_if_ALU_out_is_less_0(cpu_i_decoder_1_jmp_if_alu_out_is_less_0),
    .jmp_if_ALU_out_is_0(cpu_i_decoder_1_jmp_if_alu_out_is_0),
    .jmp_if_ALU_out_is_greater_0(cpu_i_decoder_1_jmp_if_alu_out_is_greater_0),
    .write_ALU_out_to_RAM_at_A(cpu_i_decoder_1_write_alu_out_to_ram_at_a),
    .write_ALU_out_to_D(cpu_i_decoder_1_write_alu_out_to_d),
    .write_ALU_out_to_A(cpu_i_decoder_1_write_alu_out_to_a),
    .alu_Y_if_0_A_else_RAM_at_A(cpu_i_decoder_1_alu_y_if_0_a_else_ram_at_a), .zero_X(cpu_i_decoder_1_zero_x),
    .inv_X(cpu_i_decoder_1_inv_x), .zero_Y(cpu_i_decoder_1_zero_y), .inv_Y(cpu_i_decoder_1_inv_y),
    .alu_op_if_0_logical_and_else_add(cpu_i_decoder_1_alu_op_if_0_logical_and_else_add),
    .inv_alu_out(cpu_i_decoder_1_inv_alu_out), .compute(cpu_i_decoder_1_compute),
    .value(cpu_i_decoder_1_value));
  Multiplexer #(.width(16), .enable("false")) multiplexer_1 (
    .in0(cpu_i_decoder_1_value), .in1(cpu_alu_1_output_value), .out(multiplexer_1_out),
    .sel(cpu_i_decoder_1_compute));
  cpu_memory_unit cpu_memory_unit_1 (
    .write_to_A(cpu_i_decoder_1_write_alu_out_to_a), .write_to_D(cpu_i_decoder_1_write_alu_out_to_d),
    .write_to_RAM_at_A(cpu_i_decoder_1_write_alu_out_to_ram_at_a), .value(multiplexer_1_out), .clk(clk),
    .out_A(jump_address), .out_D(cpu_memory_unit_1_out_d), .RAM_at_A(cpu_memory_unit_1_ram_at_a));
  Multiplexer #(.width(16), .enable("false")) multiplexer_2 (
    .in0(jump_address), .in1(cpu_memory_unit_1_ram_at_a), .out(multiplexer_2_out),
    .sel(cpu_i_decoder_1_alu_y_if_0_a_else_ram_at_a));
  cpu_condition cpu_condition_1 (
    .value(cpu_alu_1_output_value), .less_0(cpu_i_decoder_1_jmp_if_alu_out_is_less_0),
    .equal_0(cpu_i_decoder_1_jmp_if_alu_out_is_0), .greater_0(cpu_i_decoder_1_jmp_if_alu_out_is_greater_0),
    .jump(jump));
  cpu_alu cpu_alu_1 (
    .X(cpu_memory_unit_1_out_d), .Y(multiplexer_2_out), .zero_X(cpu_i_decoder_1_zero_x),
    .inv_X(cpu_i_decoder_1_inv_x), .zero_Y(cpu_i_decoder_1_zero_y), .inv_Y(cpu_i_decoder_1_inv_y),
    .op(cpu_i_decoder_1_alu_op_if_0_logical_and_else_add), .inv_out(cpu_i_decoder_1_inv_alu_out),
    .output_value(cpu_alu_1_output_value));
endmodule

module cpu_program (
  input  [15:0] jump_address,
  input  jump,
  input  clk,
  output [15:0] next_inst
);

  wire [15:0] cpu_counter_1_o;

  ROM #(.addrWidth(16), .dataWidth(16)) rom_1 (.addr(cpu_counter_1_o), .data(next_inst));
  cpu_counter cpu_counter_1 (.value(jump_address), .clk(clk), .store(jump), .o(cpu_counter_1_o));

  // Notes on the sheet:
  //   contents of rom_1 (hex, n*v repeats v):
  //   4 8890 5 8090 0 8288 7 8007
endmodule

module cpu (
);

  wire clock_1_out, cpu_control_unit_1_jump;
  wire [15:0] cpu_control_unit_1_jump_address, cpu_program_1_next_inst;

  Clock clock_1 (.out(clock_1_out));
  cpu_control_unit cpu_control_unit_1 (
    .clk(clock_1_out), .inst(cpu_program_1_next_inst), .jump_address(cpu_control_unit_1_jump_address),
    .jump(cpu_control_unit_1_jump));
  cpu_program cpu_program_1 (
    .jump_address(cpu_control_unit_1_jump_address), .jump(cpu_control_unit_1_jump), .clk(clock_1_out),
    .next_inst(cpu_program_1_next_inst));
endmodule
