// Logisim project cpu1.circ as structural Verilog: 7 circuits, main circuit unary_alu
module main (
);

  wire clock_1_out, instr_decoder_1_alu_invert_lhs, instr_decoder_1_alu_invert_result,
       instr_decoder_1_alu_invert_rhs, instr_decoder_1_alu_op_type, instr_decoder_1_alu_rhs_deref_a,
       instr_decoder_1_alu_zero_lhs, instr_decoder_1_alu_zero_rhs, instr_decoder_1_data_instr,
       instr_decoder_1_jump_e0, instr_decoder_1_jump_g0, instr_decoder_1_jump_l0, instr_decoder_1_store_a,
       instr_decoder_1_store_at_a, instr_decoder_1_store_d, jump_1_result;
  wire [15:0] alu_1_result, instr_decoder_1_data, memory_1_at_addr_reg_a, memory_1_reg_a, memory_1_reg_d,
       multiplexer_1_out, multiplexer_2_out, program_counter_1_instr_addr, rom_1_data;

  ROM #(.addrWidth(16), .dataWidth(16)) rom_1 (.addr(program_counter_1_instr_addr), .data(rom_1_data));
  instr_decoder instr_decoder_1 (
    .instr(rom_1_data), .jump_l0(instr_decoder_1_jump_l0), .jump_e0(instr_decoder_1_jump_e0),
    .jump_g0(instr_decoder_1_jump_g0), .store_at_A(instr_decoder_1_store_at_a),
    .store_D(instr_decoder_1_store_d), .store_A(instr_decoder_1_store_a), .data(instr_decoder_1_data),
    .data_instr(instr_decoder_1_data_instr), .alu_zero_lhs(instr_decoder_1_alu_zero_lhs),
    .alu_invert_lhs(instr_decoder_1_alu_invert_lhs), .alu_zero_rhs(instr_decoder_1_alu_zero_rhs),
    .alu_invert_rhs(instr_decoder_1_alu_invert_rhs), .alu_op_type(instr_decoder_1_alu_op_type),
    .alu_invert_result(instr_decoder_1_alu_invert_result), .alu_rhs_deref_A(instr_decoder_1_alu_rhs_deref_a));
  Multiplexer #(.width(16), .enable("false")) multiplexer_1 (
    .in0(memory_1_reg_a), .in1(memory_1_at_addr_reg_a), .out(multiplexer_1_out),
    .sel(instr_decoder_1_alu_rhs_deref_a));
  Clock clock_1 (.out(clock_1_out));
  Multiplexer #(.width(16), .enable("false")) multiplexer_2 (
    .in0(alu_1_result), .in1(instr_decoder_1_data), .out(multiplexer_2_out), .sel(instr_decoder_1_data_instr));
  jump jump_1 (
    .data(alu_1_result), .jump_l0(instr_decoder_1_jump_l0), .jump_e0(instr_decoder_1_jump_e0),
    .jump_g0(instr_decoder_1_jump_g0), .result(jump_1_result));
  memory memory_1 (
    .clk(clock_1_out), .store_at_A(instr_decoder_1_store_at_a), .store_D(instr_decoder_1_store_d),
    .store_A(instr_decoder_1_store_a), .data(multiplexer_2_out), .at_addr_reg_A(memory_1_at_addr_reg_a),
    .reg_A(memory_1_reg_a), .reg_D(memory_1_reg_d));
  alu alu_1 (
    .zero_lhs(instr_decoder_1_alu_zero_lhs), .invert_lhs(instr_decoder_1_alu_invert_lhs),
    .zero_rhs(instr_decoder_1_alu_zero_rhs), .invert_rhs(instr_decoder_1_alu_invert_rhs),
    .operation(instr_decoder_1_alu_op_type), .invert_output(instr_decoder_1_alu_invert_result),
    .lhs_operand(memory_1_reg_d), .rhs_operand(multiplexer_1_out), .result(alu_1_result));
  program_counter program_counter_1 (
    .clk(clock_1_out), .jump(jump_1_result), .jump_addr(memory_1_reg_a),
    .instr_addr(program_counter_1_instr_addr));

  // Notes on the sheet:
  //   contents of rom_1 (hex, n*v repeats v):
  //   0 8fc8 2 8c10 1 8308 1 8a00 9c10 7 81d0 28 8301 2 8fc8 0 8a00 9c10 3 8308 3 8a00 9c10 0 8a00 9088 2
  //   8a00 9dd0 8308 1 8a00 91d0 14 8304 1 8a00 9dc8 6 8007 28 8007 8007
endmodule

module unary_alu (
  input  zero_out,
  input  invert,
  input  [15:0] operand,
  output [15:0] result
);

  wire [15:0] multiplexer_1_out, not_1_out;

  Multiplexer #(.width(16), .enable("false")) multiplexer_1 (
    .in0(operand), .in1({16{1'b0}}), .out(multiplexer_1_out), .sel(zero_out));
  assign not_1_out = ~multiplexer_1_out;  // NOT_Gate not_1, 16 bits wide
  Multiplexer #(.width(16), .enable("false")) multiplexer_2 (
    .in0(multiplexer_1_out), .in1(not_1_out), .out(result), .sel(invert));
endmodule

module alu (
  input  zero_lhs,
  input  invert_lhs,
  input  zero_rhs,
  input  invert_rhs,
  input  operation,
  input  invert_output,
  input  [15:0] lhs_operand,
  input  [15:0] rhs_operand,
  output [15:0] result
);

  wire [15:0] adder_1_out, and_1_out, multiplexer_1_out, not_1_out, unary_alu_1_result, unary_alu_2_result;

  unary_alu unary_alu_1 (.zero_out(zero_lhs), .invert(invert_lhs), .operand(lhs_operand), .result(unary_alu_1_result));
  unary_alu unary_alu_2 (.zero_out(zero_rhs), .invert(invert_rhs), .operand(rhs_operand), .result(unary_alu_2_result));
  Adder #(.width(16)) adder_1 (
    .a(unary_alu_2_result), .b(unary_alu_1_result), .out(adder_1_out), .cin(1'b0));  // open: cout
  assign and_1_out = unary_alu_1_result & unary_alu_2_result;  // AND_Gate and_1, 16 bits wide
  Multiplexer #(.width(16), .enable("false")) multiplexer_1 (
    .in0(and_1_out), .in1(adder_1_out), .out(multiplexer_1_out), .sel(operation));
  Multiplexer #(.width(16), .enable("false")) multiplexer_2 (
    .in0(multiplexer_1_out), .in1(not_1_out), .out(result), .sel(invert_output));
  assign not_1_out = ~multiplexer_1_out;  // NOT_Gate not_1, 16 bits wide
endmodule

module memory (
  input  clk,
  input  store_at_A,
  input  store_D,
  input  store_A,
  input  [15:0] data,
  output [15:0] at_addr_reg_A,
  output [15:0] reg_A,
  output [15:0] reg_D
);

  Register #(.width(16)) A (.D(data), .en(store_A), .clk(clk), .Q(reg_A));  // open: clr
  Register #(.width(16)) D (.D(data), .en(store_D), .clk(clk), .Q(reg_D));  // open: clr
  RAM #(.addrWidth(16), .dataWidth(16), .trigger("falling"), .databus("bibus")) ram_1 (
    .addr(reg_A), .we(store_at_A), .oe(1'b1), .clk(clk), .din(data), .dout(at_addr_reg_A));
endmodule

module instr_decoder (
  input  [15:0] instr,
  output jump_l0,
  output jump_e0,
  output jump_g0,
  output store_at_A,
  output store_D,
  output store_A,
  output [15:0] data,
  output data_instr,
  output alu_zero_lhs,
  output alu_invert_lhs,
  output alu_zero_rhs,
  output alu_invert_rhs,
  output alu_op_type,
  output alu_invert_result,
  output alu_rhs_deref_A
);

  wire [15:5] multiplexer_1_out;

  Multiplexer #(.width(16), .enable("false")) multiplexer_1 (
    .in0({16{1'b0}}), .in1(instr),
    .out({multiplexer_1_out[15:13], alu_rhs_deref_A, alu_zero_lhs, alu_invert_lhs, alu_zero_rhs, alu_invert_rhs, alu_op_type, alu_invert_result, multiplexer_1_out[5], store_D, store_at_A, jump_g0, jump_e0, jump_l0}),
    .sel(instr[15]));
  not not_1 (data_instr, instr[15]);
  or or_1 (store_A, multiplexer_1_out[5], data_instr);

  assign data = instr;
endmodule

module jump (
  input  [15:0] data,
  input  jump_l0,
  input  jump_e0,
  input  jump_g0,
  output result
);

  wire and_1_out, and_2_out, and_3_out, comparator_1_eq, comparator_1_gt, comparator_1_lt, or_1_out;

  Comparator #(.width(16)) comparator_1 (
    .a(data), .b({16{1'b0}}), .gt(comparator_1_gt), .eq(comparator_1_eq), .lt(comparator_1_lt));
  and and_1 (and_1_out, comparator_1_lt, jump_l0);
  and and_2 (and_2_out, comparator_1_eq, jump_e0);
  and and_3 (and_3_out, comparator_1_gt, jump_g0);
  or or_1 (or_1_out, and_1_out, and_2_out);
  or or_2 (result, or_1_out, and_3_out);
endmodule

module program_counter (
  input  clk,
  input  jump,
  input  [15:0] jump_addr,
  output [15:0] instr_addr
);

  wire [15:0] adder_1_out, multiplexer_1_out;

  Register #(.width(16)) register_1 (.D(multiplexer_1_out), .en(1'b1), .clk(clk), .Q(instr_addr));  // open: clr
  Multiplexer #(.width(16), .enable("false")) multiplexer_1 (
    .in0(adder_1_out), .in1(jump_addr), .out(multiplexer_1_out), .sel(jump));
  Adder #(.width(16)) adder_1 (.a(instr_addr), .b(16'h1), .out(adder_1_out));  // open: cin, cout
endmodule
